# Fritzing sketch Wiring (saved by Fritzing 1.0.1rc)

parts:
  NEOPIXEL1 = Neopixel Strip -- Black (30/m)
  WeMos_D1_Mini1 = WeMos D1 Mini
  JP1 = USB_MICROB_PLUG [package=micro-b-smt]
  LED2 = LED - 3mm [color="Red (633nm)" current=0.030 package="3 mm [THT]"]
  R1 = Resistor [tolerance=±5% power=0.25 resistance=15 package=THT]
  C2 = Capacitor Polarized [package=cpol-radial-100uf-25v]
  NEOPIXEL2 = Neopixel Strip -- Black (30/m)
  NEOPIXEL3 = Neopixel Strip -- Black (30/m)

nets:
  N1: NEOPIXEL1.+5V#1, JP1.D+
  N2: NEOPIXEL1.DI, WeMos_D1_Mini1.D4
  N3: NEOPIXEL1.GND#3, C2.-
  N4: NEOPIXEL1.GND#4, NEOPIXEL2.GND#3
  N5: NEOPIXEL1.DO, NEOPIXEL2.DI
  N6: NEOPIXEL1.+5V#6, NEOPIXEL2.+5V#1
  N7: WeMos_D1_Mini1.D2, R1.Pin_0
  N8: WeMos_D1_Mini1.G, JP1.VCC, LED2.cathode
  N9: LED2.anode, R1.Pin_1
  N10: NEOPIXEL2.GND#4, NEOPIXEL3.GND
  N11: NEOPIXEL2.DO, NEOPIXEL3.DI
  N12: NEOPIXEL2.+5V#6, NEOPIXEL3.+5V

notes:
  Positionslicht
  LED Band Uhranzeige
  LED Restaurant unten
  LED Restaurant oben

custom parts:
  Neopixel Strip -- Black (30/m): Neopixel Strip, Black, 30 pixels per meter.
