# Fritzing sketch Wiring (saved by Fritzing 1.0.1rc)

parts:
  NEOPIXEL1 = Neopixel Strip -- Black (30/m)
  WeMos_D1_Mini1 = WeMos D1 Mini
  JP1 = USB_MICROB_PLUG [package=micro-b-smt]
  LED2 = LED - 3mm [color="Red (633nm)" current=0.030 package="3 mm [THT]"]
  22_Ohm = Resistor [tolerance=±5% power=0.25 resistance=22 package=THT]
  100µF = Capacitor Polarized [package=cpol-radial-100uf-25v]
  NEOPIXEL2 = Neopixel Strip -- Black (30/m)
  NEOPIXEL3 = Neopixel Strip -- Black (30/m)
  A1 = Esp32-c3 super mini  # not connected
  R2 = Resistor [tolerance=±5% power=0.25 resistance=470 package=THT]

nets:
  N1: NEOPIXEL1.+5V#1, JP1.D+
  N2: NEOPIXEL1.DI, R2.Pin_1
  N3: NEOPIXEL1.GND#3, 100µF.-
  N4: NEOPIXEL1.GND#4, NEOPIXEL2.GND#3
  N5: NEOPIXEL1.DO, NEOPIXEL2.DI
  N6: NEOPIXEL1.+5V#6, NEOPIXEL2.+5V#1
  N7: WeMos_D1_Mini1.D2, 22_Ohm.Pin_0
  N8: WeMos_D1_Mini1.D4, R2.Pin_0
  N9: WeMos_D1_Mini1.G, JP1.VCC, LED2.cathode
  N10: LED2.anode, 22_Ohm.Pin_1
  N11: NEOPIXEL2.GND#4, NEOPIXEL3.GND
  N12: NEOPIXEL2.DO, NEOPIXEL3.DI
  N13: NEOPIXEL2.+5V#6, NEOPIXEL3.+5V

notes:
  Positionslicht
  LED Band Uhranzeige
  LED Restaurant unten
  LED Restaurant oben
  Wemos D1 mini
  ESP 32 C3 super mini

custom parts:
  Neopixel Strip -- Black (30/m): Neopixel Strip, Black, 30 pixels per meter.
  Esp32-c3 super mini: ESP32-C3 Development Board ESP32 SuperMini Development Board ESP32 Development Board WiFi Bluetooth.
